// Logisim project realAlu.circ as structural Verilog
module AND (
  input  [7:0] A,
  input  [7:0] B,
  output [7:0] out_3
);

  assign out_3 = A & B;  // AND_Gate and_1, 8 bits wide
endmodule

module OR (
  input  [7:0] A,
  input  [7:0] B,
  output [7:0] out_3
);

  assign out_3 = A | B;  // OR_Gate or_1, 8 bits wide
endmodule

module HA (
  input  in_1,
  input  in_2,
  output out_3,
  output out_4
);

  xor xor_1 (out_3, in_2, in_1);
  and and_1 (out_4, in_2, in_1);
endmodule

module FA (
  input  in_1,
  input  in_2,
  input  in_3,
  output out_4,
  output out_5
);

  wire and_1_out, and_2_out, and_3_out, xor_1_out;

  and and_1 (and_1_out, in_3, in_2);
  and and_2 (and_2_out, in_3, in_1);
  and and_3 (and_3_out, in_2, in_1);
  xor xor_1 (xor_1_out, in_3, in_2);
  xor xor_2 (out_4, xor_1_out, in_1);
  or or_1 (out_5, and_1_out, and_2_out, and_3_out);
endmodule

module Adder_4bits (
  input  in_1,
  input  in_2,
  input  in_3,
  input  in_4,
  input  in_5,
  input  in_6,
  input  in_7,
  input  in_8,
  input  in_9,
  output out_10,
  output out_11,
  output out_12,
  output out_13,
  output out_14
);

  wire fa_1_out_5, fa_2_out_5, fa_3_out_5;

  FA fa_1 (.out_4(out_10), .out_5(fa_1_out_5), .in_1(in_3), .in_2(in_2), .in_3(in_1));
  FA fa_2 (.out_4(out_11), .out_5(fa_2_out_5), .in_1(fa_1_out_5), .in_2(in_5), .in_3(in_4));
  FA fa_3 (.out_4(out_12), .out_5(fa_3_out_5), .in_1(fa_2_out_5), .in_2(in_7), .in_3(in_6));
  FA fa_4 (.out_4(out_13), .out_5(out_14), .in_1(fa_3_out_5), .in_2(in_9), .in_3(in_8));
endmodule

module Adder_8_bits (
  input  in_1,
  input  in_2,
  input  in_3,
  input  in_4,
  input  in_5,
  input  in_6,
  input  in_7,
  input  in_8,
  input  in_9,
  input  in_10,
  input  in_11,
  input  in_12,
  input  in_13,
  input  in_14,
  input  in_15,
  input  in_16,
  output out_17,
  output out_18,
  output out_19,
  output out_20,
  output out_21,
  output out_22,
  output out_23,
  output out_24,
  output out_25
);

  wire adder_4bits_2_out_14;

  Adder_4bits adder_4bits_1 (
    .out_10(out_21), .out_11(out_20), .out_12(out_19), .out_13(out_18), .in_1(in_7), .in_4(in_5),
    .in_6(in_3), .in_8(in_1), .in_2(in_8), .in_5(in_6), .in_7(in_4), .in_9(in_2),
    .in_3(adder_4bits_2_out_14), .out_14(out_17));
  Adder_4bits adder_4bits_2 (
    .out_10(out_25), .out_11(out_24), .out_12(out_23), .out_13(out_22), .in_1(in_15), .in_4(in_13),
    .in_6(in_11), .in_8(in_9), .in_2(in_16), .in_5(in_14), .in_7(in_12), .in_9(in_10), .in_3(1'b0),
    .out_14(adder_4bits_2_out_14));
endmodule

module NOT_B (
  input  [7:0] B,
  output [7:0] out_2
);

  assign out_2 = ~B;  // NOT_Gate not_1, 8 bits wide
endmodule
